# Fritzing sketch APRSWXBox (saved by Fritzing 0.7.4b)

parts:
  Arduino1 = Arduino  # not connected
  Arduino_Ethernet_Shield1 = Arduino Ethernet Shield
  RHT1 = Humidity and Temperature Sensor RHT03
  元件1 = Barometric Pressure Sensor - BMP085 Breakout

nets:
  N1: Arduino_Ethernet_Shield1.D3, RHT1.Data-signal
  3V3: Arduino_Ethernet_Shield1.3V3, 元件1.VCC
  +5V: Arduino_Ethernet_Shield1.+5V, RHT1.Vcc
  N2: Arduino_Ethernet_Shield1.GND#19, RHT1.GND_2
  N3: Arduino_Ethernet_Shield1.GND#20, 元件1.GND
  N4: Arduino_Ethernet_Shield1.A4, 元件1.SDA
  N5: Arduino_Ethernet_Shield1.A5, 元件1.SCL

notes:
  BMP085
  SDA,SCL,GND,VCC
